// Logisim project ADD_1.circ as structural Verilog: 2 circuits, main circuit main
module main (
  input  in_1,
  input  in_2,
  input  in_3
);
endmodule

module ADD_1 (
  input  A,
  input  B,
  input  C,
  output out_4,
  output out_5
);

  wire and_1_out, and_2_out, or_1_out, xor_1_out;

  xor xor_1 (xor_1_out, A, B);
  xor xor_2 (out_4, xor_1_out, C);
  or or_1 (or_1_out, B, C);
  and and_1 (and_1_out, or_1_out, A);
  and and_2 (and_2_out, B, C);
  or or_2 (out_5, and_1_out, and_2_out);
endmodule
